# Fritzing sketch Alarm (saved by Fritzing 0.9.3b)

parts:
  LCD1 = LCD screen
  Εξάρτημα1 = Arduino Mega ADK (Rev3)
  U1 = POT [package=pot_alpha_rv16af-20]
  Matrix_keypad1 = KEYPAD 4x4
  J1 = Piezo Speaker
  LED1 = LED - 5mm [color="Red (633nm)" package="5 mm [THT]"]
  LED3 = LED - 5mm [color="Green (565nm)" package="5 mm [THT]"]
  S1 = Square Pushbutton
  R1 = Resistor [tolerance=±5% resistance=1M package="1206 [SMD]"]

nets:
  VSS: LCD1.VSS, LCD1.R/W, Εξάρτημα1.GND, J1.pin1, LED1.anode, LED3.anode
  VDD: LCD1.VDD, Εξάρτημα1.5V, U1.A, R1.Pin_0
  N1: LCD1.V0, U1.S
  N2: LCD1.RS, Εξάρτημα1.D41
  N3: LCD1.E, Εξάρτημα1.D40
  N4: LCD1.DB4, Εξάρτημα1.D45
  N5: LCD1.DB5, Εξάρτημα1.D44
  N6: LCD1.DB6, Εξάρτημα1.D43
  N7: LCD1.DB7, Εξάρτημα1.D42
  N8: LCD1.LED+, R1.Pin_1
  N9: LCD1.LED-, U1.E
  N10: Εξάρτημα1.AREF, S1.leg1
  N11: Εξάρτημα1.D13_PWM, S1.leg0
  N12: Εξάρτημα1.D9_PWM, Matrix_keypad1.row4
  N13: Εξάρτημα1.D8_PWM, Matrix_keypad1.row3
  N14: Εξάρτημα1.D2_PWM, Matrix_keypad1.col1
  N15: Εξάρτημα1.D3_PWM, Matrix_keypad1.col2
  N16: Εξάρτημα1.D4_PWM, Matrix_keypad1.col3
  N17: Εξάρτημα1.D5_PWM, Matrix_keypad1.col4
  N18: Εξάρτημα1.D6_PWM, Matrix_keypad1.row1
  N19: Εξάρτημα1.D7_PWM, Matrix_keypad1.row2
  N20: Εξάρτημα1.D46, J1.pin2
  N21: Εξάρτημα1.D48, LED3.cathode
  N22: Εξάρτημα1.D49, LED1.cathode

custom parts:
  KEYPAD 4x4: Matrix keypad 16 buttons, 4 rows x 4 columns
