# Fritzing sketch Ethernet (saved by Fritzing 0.9.3b)
breadboards: 1

parts:
  Part1 = Arduino Uno (Rev3) - ICSP  # not connected
  Part2 = Arduino Uno (Rev3) - ICSP
  Part3 = Arduino Mega ADK (Rev3)
  Q1 = NPN-Transistor [package="TO92 [THT]"]
  Q2 = NPN-Transistor [package="TO92 [THT]"]
  Q3 = NPN-Transistor [package="TO92 [THT]"]
  R1 = Resistor [tolerance=±5% resistance=330 package="0402 [SMD]"]
  R2 = Resistor [tolerance=±5% resistance=330 package="0402 [SMD]"]
  R3 = Resistor [tolerance=±5% resistance=330 package="0402 [SMD]"]
  Part4 = Arduino Ethernet Shield (Rev3)

nets:
  GND: Part2.GND, Part3.GND, R1.Pin_1, R2.Pin_1, R3.Pin_1, Part4.GND
  N1: Part2.D7, Q3.B
  N2: Part3.D34, Q2.B
  N3: Part3.D36, Q1.B
  N4: Q1.E, Part4.SDCS
  N5: Q1.C, R1.Pin_0
  N6: Q2.E, Part4.D7
  N7: Q2.C, R2.Pin_0
  N8: Q3.E, Part4.D8
  N9: Q3.C, R3.Pin_0
