# Fritzing sketch Sensors (saved by Fritzing 0.9.3b)

parts:
  Εξάρτημα4 = Arduino Uno (Rev3)
  FC-2 = Sound Sensor
  IC2 = L293D [package=THT]
  Εξάρτημα5 = songle relay
  D2 = LTE-302 [package=lte-302]
  R3 = PHOTOCELL [package=photocell-kit]
  R4 = Resistor [tolerance=±5% resistance=1k package=THT]
  LED6 = LED - 3mm [color="Green (560nm)" package="3 mm [THT]"]
  LED7 = LED - 3mm [color="Red (633nm)" package="3 mm [THT]"]
  Εξάρτημα6 = MQ-4

nets:
  N1: Εξάρτημα4.A0, R3.P$2, R4.Pin_1
  N2: Εξάρτημα4.A1, Εξάρτημα6.AO
  N3: Εξάρτημα4.A3, FC-2.OUT
  N4: Εξάρτημα4.D12/MISO, LED7.anode
  N5: Εξάρτημα4.D13/SCK, LED6.anode
  GND: Εξάρτημα4.GND, D2.A, R4.Pin_0, LED7.cathode, Εξάρτημα6.GND
  N6: Εξάρτημα4.D3_PWM, IC2.In_2
  N7: Εξάρτημα4.D4, IC2.In_1
  N8: Εξάρτημα4.D5_PWM, IC2.Enable_1
  5V: Εξάρτημα4.5V, FC-2.VCC, R3.P$1
  N9: FC-2.GND, LED6.cathode
  N10: IC2.Out_1_(_Controlled_by_Enable_1_), Εξάρτημα5.GND
  N11: IC2.Out_2_(_Controlled_by_Enable_1_), Εξάρτημα5.VCC
  N12: IC2.+Vmotor, Εξάρτημα5.COMMON
  N13: Εξάρτημα5.NO, D2.C
